// Logisim project Design.circ as structural Verilog: 11 circuits, main circuit main
module main (
  output [31:0] out_1,
  output [31:0] out_2,
  output [31:0] out_3,
  output [31:0] out_4,
  output [31:0] out_5,
  output [4:0] out_6,
  output [31:0] out_7,
  output [31:0] out_8,
  output [31:0] out_9,
  output [31:0] out_10
);

  wire alu_1_zero, and_1_out, and_2_out, clock_1_out, clock_2_out, clock_3_out, MemR_ALU, MemR_EXEC,
       MemW_EXEC, not_1_out, not_2_out, not_3_out, not_4_out, or_1_out, pc_src, Reg_WR_EXEC, register_1_q,
       src1, Stall, WB_REG_WR, ZERO_q;
  wire [0:0] MEM_EXEC_q;
  wire [1:0] fowardab_1_fa, fowardab_1_fb, MEM_EX_q, WB_EX_q;
  wire [1:1] register_2_q, WB_EXEC_q;
  wire [2:0] alucontrol_1_s, fun3_EX;
  wire [2:1] EX_q;
  wire [4:0] IR_q_2, IR_q_3, RD_EXEC_q, rd_ID_EX;
  wire [7:0] controlunit_1_flags, multiplexer_1_out;
  wire [23:0] PC_q;
  wire [31:0] A_DEC_q, adder_1_out, B_DEC_q, B_EXEC_q, bAddress_q, bit_extender_1_out, C, C_q,
       igu_1_immediate, IM_data, IMM_q, IR_q, MDR_q, multiplexer_2_out, multiplexer_3_out, multiplexer_4_out,
       PC_FETCH_q, ram_1_dout, rf_1_rd1, rf_1_rd2;

  Counter #(.max('hffffff), .width(24)) PC (
    .load(pc_src), .count(not_1_out), .clk(clock_1_out), .D(bAddress_q[23:0]), .Q(PC_q));  // open: clr, up, carry
  Clock clock_1 (.out(clock_1_out));
  not not_1 (not_1_out, Stall);
  ROM #(.addrWidth(24), .dataWidth(32)) IM (.addr(PC_q), .data(IM_data));
  assign bit_extender_1_out = {{8{1'b0}}, PC_q};  // Bit_Extender bit_extender_1
  Clock clock_2 (.out(clock_2_out));
  Register #(.width(32)) PC_FETCH (
    .D(bit_extender_1_out), .en(not_2_out), .clk(clock_2_out), .Q(PC_FETCH_q));  // open: clr
  not not_2 (not_2_out, Stall);
  Register #(.width(32)) IR (
    .D(IM_data), .en(not_2_out), .clk(clock_2_out), .Q({IR_q[31:25], IR_q_3, IR_q_2, IR_q[14:0]}),
    .clr(pc_src));
  ControlUnit controlunit_1 (.op(IR_q[6:0]), .flags(controlunit_1_flags));
  HDU hdu_1 (.rs1_IF_ID(IR_q_2), .rs2_IF_ID(IR_q_3), .rd_ID_Ex(rd_ID_EX), .MemR_ID_EX(MemR_ALU), .Stall(Stall));
  Multiplexer #(.width(8)) multiplexer_1 (
    .in0(controlunit_1_flags), .in1({8{1'b0}}), .out(multiplexer_1_out), .sel(or_1_out));
  or or_1 (or_1_out, pc_src, Stall);
  RF rf_1 (
    .RR1(IR_q_2), .RR2(IR_q_3), .WD(out_4), .WE(WB_REG_WR), .WR(out_6), .clk(clock_2_out), .x1(out_7),
    .x2(out_8), .x3(out_9), .x4(out_10), .RD1(rf_1_rd1), .RD2(rf_1_rd2));
  Register #(.width(2)) WB_EX (.D(multiplexer_1_out[1:0]), .en(1'b1), .clk(clock_2_out), .Q(WB_EX_q), .clr(pc_src));
  Register #(.width(3)) MEM_EX (
    .D(multiplexer_1_out[4:2]), .en(1'b1), .clk(clock_2_out), .Q({MemR_ALU, MEM_EX_q}), .clr(pc_src));
  Register #(.width(3)) EX (.D(multiplexer_1_out[7:5]), .en(1'b1), .clk(clock_2_out), .Q({EX_q, src1}));  // open: clr
  Register #(.width(32)) PC_EXECUTE (.D(PC_FETCH_q), .en(1'b1), .clk(clock_2_out), .Q(out_2));  // open: clr
  Register #(.width(32)) A_DEC (.D(rf_1_rd1), .en(1'b1), .clk(clock_2_out), .Q(A_DEC_q));  // open: clr
  Register #(.width(32)) B_DEC (.D(rf_1_rd2), .en(1'b1), .clk(clock_2_out), .Q(B_DEC_q));  // open: clr
  Register #(.width(32)) IMM (
    .D({IR_q[31:25], IR_q_3, IR_q_2, IR_q[14:0]}), .en(1'b1), .clk(clock_2_out),
    .Q({IMM_q[31:15], fun3_EX, rd_ID_EX, IMM_q[6:0]}));  // open: clr
  IGU igu_1 (.Instruction({IMM_q[31:15], fun3_EX, rd_ID_EX, IMM_q[6:0]}), .S(EX_q), .Immediate(igu_1_immediate));
  Multiplexer #(.select(2), .width(32)) multiplexer_2 (
    .in0(A_DEC_q), .in1(C), .in2(out_4), .out(multiplexer_2_out), .sel(fowardab_1_fa));  // open: in3
  Multiplexer #(.select(2), .width(32)) multiplexer_3 (
    .in0(B_DEC_q), .in1(C), .in2(out_4), .out(multiplexer_3_out), .sel(fowardab_1_fb));  // open: in3
  FowardAB fowardab_1 (
    .rs1_ID_Ex(IMM_q[19:15]), .rs2_ID_Ex(IMM_q[24:20]), .rd_Ex_Mem(RD_EXEC_q), .Mem_WB_rd(out_6),
    .RegWr_Ex_Mem(Reg_WR_EXEC), .Mem_WB_RegWr(WB_REG_WR), .Fa(fowardab_1_fa), .Fb(fowardab_1_fb));
  Multiplexer #(.width(32)) multiplexer_4 (
    .in0(multiplexer_3_out), .in1(igu_1_immediate), .out(multiplexer_4_out), .sel(src1));
  Divider #(.width(32)) divider_1 (.a(igu_1_immediate), .b(32'h4), .out(out_1));  // open: upper, rem
  ALU alu_1 (.A(multiplexer_2_out), .B(multiplexer_4_out), .OP(alucontrol_1_s), .ALUOUT(out_3), .Zero(alu_1_zero));
  ALUcontrol alucontrol_1 (.op(IMM_q[6:0]), .func3(fun3_EX), .func7(IMM_q[31:25]), .S(alucontrol_1_s));
  Adder #(.width(32)) adder_1 (.a(out_2), .b(out_1), .out(adder_1_out));  // open: cin, cout
  Register #(.width(2)) WB_EXEC (
    .D(WB_EX_q), .en(1'b1), .clk(clock_2_out), .Q({WB_EXEC_q[1], Reg_WR_EXEC}));  // open: clr
  Register #(.width(3)) MEM_EXEC (
    .D({MemR_ALU, MEM_EX_q}), .en(1'b1), .clk(clock_2_out), .Q({MemR_EXEC, MemW_EXEC, MEM_EXEC_q[0]}));  // open: clr
  Register #(.width(32)) bAddress (.D(adder_1_out), .en(1'b1), .clk(clock_2_out), .Q(bAddress_q));  // open: clr
  Register #(.width(1)) register_1 (.D(fun3_EX[0]), .en(1'b1), .clk(clock_2_out), .Q(register_1_q));  // open: clr
  Register #(.width(1)) ZERO (.D(alu_1_zero), .en(1'b1), .clk(clock_2_out), .Q(ZERO_q));  // open: clr
  Register #(.width(32)) C_EXEC (.D(out_3), .en(1'b1), .clk(clock_2_out), .Q(C));  // open: clr
  Register #(.width(32)) B_EXEC (.D(B_DEC_q), .en(1'b1), .clk(clock_2_out), .Q(B_EXEC_q));  // open: clr
  Register #(.width(5)) RD_EXEC (.D(rd_ID_EX), .en(1'b1), .clk(clock_2_out), .Q(RD_EXEC_q));  // open: clr
  not not_3 (not_3_out, ZERO_q);
  not not_4 (not_4_out, register_1_q);
  and and_1 (and_1_out, MEM_EXEC_q[0], register_1_q, not_3_out);
  and and_2 (and_2_out, MEM_EXEC_q[0], not_4_out, ZERO_q);
  or or_2 (pc_src, and_1_out, and_2_out);
  RAM #(.addrWidth(24), .dataWidth(32)) ram_1 (
    .addr(C[23:0]), .we(MemW_EXEC), .oe(MemR_ALU), .clk(clock_2_out), .din(B_EXEC_q), .dout(ram_1_dout));
  Clock clock_3 (.out(clock_3_out));
  Register #(.width(2)) register_2 (
    .D({WB_EXEC_q[1], Reg_WR_EXEC}), .en(1'b1), .clk(clock_3_out), .Q({register_2_q[1], WB_REG_WR}));  // open: clr
  Register #(.width(32)) MDR (.D(ram_1_dout), .en(1'b1), .clk(clock_3_out), .Q(MDR_q));  // open: clr
  Register #(.width(32)) u_C (.D(C), .en(1'b1), .clk(clock_3_out), .Q(C_q));  // open: clr
  Register #(.width(5)) register_3 (.D(RD_EXEC_q), .en(1'b1), .clk(clock_3_out), .Q(out_6));  // open: clr
  Multiplexer #(.width(32)) multiplexer_5 (.in0(C_q), .in1(MDR_q), .out(out_4), .sel(register_2_q[1]));

  assign out_5 = out_4;

  // Other names for the same wires on the sheet: x1[31:0] = out_7; x2[31:0] = out_8; x3[31:0] = out_9;
  //   x4[31:0] = out_10; Y[31:0] = out_4

  // Notes on the sheet:
  //   contents of IM (hex, n*v repeats v):
  //   a00093 500113 6*33 2081b3 1181b3 2181b3 5*33 302023 5*33 2203 a20213 5*33 508093 fe121ee3 8*33
endmodule

module ALU (
  input  [31:0] A,
  input  [31:0] B,
  input  [2:0] OP,
  output [31:0] ALUOUT,
  output Zero
);

  wire adder_1_cout, and_3_out, and_4_out, not_2_out, not_3_out, not_4_out, not_5_out, or_2_out, or_3_out,
       or_4_out, S, SLT, SUB_SYM;
  wire [30:0] adder_1_out;
  wire [31:0] and_1_out, bit_extender_1_out, bit_extender_2_out, multiplexer_1_out, not_1_out, or_1_out,
       xor_1_out;

  assign and_1_out = A & B;  // AND_Gate and_1, 32 bits wide
  assign or_1_out = A | B;  // OR_Gate or_1, 32 bits wide
  assign xor_1_out = A ^ B;  // XOR_Gate xor_1, 32 bits wide
  assign not_1_out = ~B;  // NOT_Gate not_1, 32 bits wide
  Multiplexer #(.width(32)) multiplexer_1 (.in0(B), .in1(not_1_out), .out(multiplexer_1_out), .sel(SUB_SYM));
  or or_2 (or_2_out, OP[1], OP[0]);
  and and_2 (SUB_SYM, OP[2], or_2_out);
  Adder #(.width(32)) adder_1 (
    .a(A), .b(multiplexer_1_out), .out({S, adder_1_out}), .cin(SUB_SYM), .cout(adder_1_cout));
  not not_2 (not_2_out, A[31]);
  not not_3 (not_3_out, B[31]);
  not not_4 (not_4_out, S);
  not not_5 (not_5_out, adder_1_cout);
  assign bit_extender_1_out = {{31{1'b0}}, SLT};  // Bit_Extender bit_extender_1
  assign bit_extender_2_out = {{31{1'b0}}, not_5_out};  // Bit_Extender bit_extender_2
  and and_3 (and_3_out, not_2_out, not_3_out, S);
  and and_4 (and_4_out, A[31], B[31], not_4_out);
  Multiplexer #(.select(3), .width(32)) multiplexer_2 (
    .in0(and_1_out), .in1(or_1_out), .in2(xor_1_out), .in3(B), .in4({S, adder_1_out}),
    .in5({S, adder_1_out}), .in6(bit_extender_1_out), .in7(bit_extender_2_out), .out(ALUOUT), .sel(OP));
  or or_3 (or_3_out, and_3_out, and_4_out);
  xor xor_2 (SLT, or_3_out, S);
  or or_4 (or_4_out, ALUOUT[31], ALUOUT[30], ALUOUT[29], ALUOUT[28], ALUOUT[27], ALUOUT[26], ALUOUT[25], ALUOUT[24], ALUOUT[23], ALUOUT[22], ALUOUT[21], ALUOUT[20], ALUOUT[19], ALUOUT[18], ALUOUT[17], ALUOUT[16], ALUOUT[15], ALUOUT[14], ALUOUT[13], ALUOUT[12], ALUOUT[11], ALUOUT[10], ALUOUT[9], ALUOUT[8], ALUOUT[7], ALUOUT[6], ALUOUT[5], ALUOUT[4], ALUOUT[3], ALUOUT[2], ALUOUT[1], ALUOUT[0]);
  not not_6 (Zero, or_4_out);
endmodule

module IGU (
  input  [31:0] Instruction,
  input  [1:0] S,
  output [31:0] Immediate
);

  wire [31:0] bit_extender_1_out, bit_extender_2_out, bit_extender_3_out;

  assign bit_extender_1_out = {{20{Instruction[31]}}, Instruction[31:20]};  // Bit_Extender bit_extender_1
  assign bit_extender_2_out = {{20{Instruction[31]}}, {Instruction[31:25], Instruction[11:7]}};  // Bit_Extender bit_extender_2
  assign bit_extender_3_out = {{19{Instruction[31]}}, {Instruction[31], Instruction[7], Instruction[30:25], Instruction[11:8], 1'b0}};  // Bit_Extender bit_extender_3
  Multiplexer #(.select(2), .width(32)) multiplexer_1 (
    .in0(bit_extender_1_out), .in1(bit_extender_2_out), .in2(bit_extender_3_out), .out(Immediate), .sel(S));  // open: in3
endmodule

module RF (
  input  [4:0] RR1,
  input  [4:0] RR2,
  input  [31:0] WD,
  input  WE,
  input  [4:0] WR,
  input  clk,
  output [31:0] x1,
  output [31:0] x2,
  output [31:0] x3,
  output [31:0] x4,
  output [31:0] RD1,
  output [31:0] RD2
);

  wire and_1_out, and_2_out, and_3_out, and_4_out, and_5_out, and_6_out, and_7_out, and_8_out, and_9_out,
       and_10_out, and_11_out, and_12_out, and_13_out, and_14_out, and_15_out, and_16_out, and_17_out,
       and_18_out, and_19_out, and_20_out, and_21_out, and_22_out, and_23_out, and_24_out, and_25_out,
       and_26_out, and_27_out, and_28_out, and_29_out, and_30_out, and_31_out, and_32_out, E1, E2, E3, E4,
       E5, E6, E7, E8, E9, E10, E11, E12, E13, E14, E15, E16, E17, E18, E19, E20, E21, E22, E23, E24, E25,
       E26, E27, E28, E29, E30, E31, E32, undriven, undriven_2, undriven_3, undriven_4, undriven_5,
       undriven_6, undriven_7, undriven_8, undriven_9, undriven_10, undriven_11, undriven_12, undriven_13,
       undriven_14, undriven_15, undriven_16, undriven_17, undriven_18, undriven_19, undriven_20, undriven_21;
  wire [31:0] R1, R6, R7, R8, R9, R10, R11, R12, R13, R14, R15, R16, R17, R18, R19, R20, R21, R22, R23, R24,
       R25, R26, R27, R28, R29, R30, R31, R32;

  Decoder #(.select(5)) decoder_1 (
    .out0(E1), .out1(E2), .out2(E3), .out3(E4), .out4(E5), .out5(E6), .out6(E7), .out7(E8), .out8(E9),
    .out9(E10), .out10(E11), .out11(E12), .out12(E13), .out13(E14), .out14(E15), .out15(E16), .out16(E17),
    .out17(E18), .out18(E19), .out19(E20), .out20(E21), .out21(E22), .out22(E23), .out23(E24), .out24(E25),
    .out25(E26), .out26(E27), .out27(E28), .out28(E29), .out29(E30), .out30(E31), .out31(E32), .sel(WR));  // open: en
  and and_1 (and_1_out, E1, WE);
  and and_2 (and_2_out, E2, WE);
  and and_3 (and_3_out, E3, WE);
  and and_4 (and_4_out, E4, WE);
  and and_5 (and_5_out, E5, WE);
  and and_6 (and_6_out, E6, WE);
  and and_7 (and_7_out, E7, WE);
  and and_8 (and_8_out, E8, WE);
  and and_9 (and_9_out, E9, WE);
  and and_10 (and_10_out, E10, WE);
  and and_11 (and_11_out, E11, WE);
  and and_12 (and_12_out, E12, WE);
  and and_13 (and_13_out, E13, WE);
  and and_14 (and_14_out, E14, WE);
  and and_15 (and_15_out, E15, WE);
  and and_16 (and_16_out, E16, WE);
  and and_17 (and_17_out, E17, WE);
  and and_18 (and_18_out, E18, WE);
  and and_19 (and_19_out, E19, WE);
  and and_20 (and_20_out, E20, WE);
  and and_21 (and_21_out, E21, WE);
  and and_22 (and_22_out, E22, WE);
  and and_23 (and_23_out, E23, WE);
  and and_24 (and_24_out, E24, WE);
  and and_25 (and_25_out, E25, WE);
  and and_26 (and_26_out, E26, WE);
  and and_27 (and_27_out, E27, WE);
  and and_28 (and_28_out, E28, WE);
  and and_29 (and_29_out, E29, WE);
  and and_30 (and_30_out, E30, WE);
  and and_31 (and_31_out, E31, WE);
  and and_32 (and_32_out, E32, WE);
  Register #(.width(32)) register_1 (.D({32{1'b0}}), .en(and_1_out), .clk(clk), .Q(R1), .clr(undriven));
  Register #(.width(32)) register_2 (.D(WD), .en(and_2_out), .clk(clk), .Q(x1), .clr(undriven_2));
  Register #(.width(32)) register_3 (.D(WD), .en(and_3_out), .clk(clk), .Q(x2), .clr(undriven_3));
  Register #(.width(32)) register_4 (.D(WD), .en(and_4_out), .clk(clk), .Q(x3), .clr(undriven_4));
  Register #(.width(32)) register_5 (.D(WD), .en(and_5_out), .clk(clk), .Q(x4), .clr(undriven_5));
  Register #(.width(32)) register_6 (.D(WD), .en(and_6_out), .clk(clk), .Q(R6), .clr(undriven_6));
  Register #(.width(32)) register_7 (.D(WD), .en(and_7_out), .clk(clk), .Q(R7), .clr(undriven_7));
  Register #(.width(32)) register_8 (.D(WD), .en(and_8_out), .clk(clk), .Q(R8), .clr(undriven_8));
  Register #(.width(32)) register_9 (.D(WD), .en(and_9_out), .clk(clk), .Q(R9), .clr(undriven_9));
  Register #(.width(32)) register_10 (.D(WD), .en(and_10_out), .clk(clk), .Q(R10), .clr(undriven_10));
  Register #(.width(32)) register_11 (.D(WD), .en(and_11_out), .clk(clk), .Q(R11), .clr(undriven_11));
  Register #(.width(32)) register_12 (.D(WD), .en(and_12_out), .clk(clk), .Q(R12), .clr(undriven_12));
  Register #(.width(32)) register_13 (.D(WD), .en(and_13_out), .clk(clk), .Q(R13), .clr(undriven_13));
  Register #(.width(32)) register_14 (.D(WD), .en(and_14_out), .clk(clk), .Q(R14), .clr(undriven_14));
  Register #(.width(32)) register_15 (.D(WD), .en(and_15_out), .clk(clk), .Q(R15), .clr(undriven_15));
  Register #(.width(32)) register_16 (.D(WD), .en(and_16_out), .clk(clk), .Q(R16), .clr(undriven_16));
  Register #(.width(32)) register_17 (.D(WD), .en(and_17_out), .clk(clk), .Q(R17), .clr(undriven_17));
  Register #(.width(32)) register_18 (.D(WD), .en(and_18_out), .clk(clk), .Q(R18), .clr(undriven_18));
  Register #(.width(32)) register_19 (.D(WD), .en(and_19_out), .clk(clk), .Q(R19), .clr(undriven_19));
  Register #(.width(32)) register_20 (.D(WD), .en(and_20_out), .clk(clk), .Q(R20), .clr(undriven_20));
  Register #(.width(32)) register_21 (.D(WD), .en(and_21_out), .clk(clk), .Q(R21), .clr(undriven_21));
  Register #(.width(32)) register_22 (.D(WD), .en(and_22_out), .clk(clk), .Q(R22));  // open: clr
  Register #(.width(32)) register_23 (.D(WD), .en(and_23_out), .clk(clk), .Q(R23));  // open: clr
  Register #(.width(32)) register_24 (.D(WD), .en(and_24_out), .clk(clk), .Q(R24));  // open: clr
  Register #(.width(32)) register_25 (.D(WD), .en(and_25_out), .clk(clk), .Q(R25));  // open: clr
  Register #(.width(32)) register_26 (.D(WD), .en(and_26_out), .clk(clk), .Q(R26));  // open: clr
  Register #(.width(32)) register_27 (.D(WD), .en(and_27_out), .clk(clk), .Q(R27));  // open: clr
  Register #(.width(32)) register_28 (.D(WD), .en(and_28_out), .clk(clk), .Q(R28));  // open: clr
  Register #(.width(32)) register_29 (.D(WD), .en(and_29_out), .clk(clk), .Q(R29));  // open: clr
  Register #(.width(32)) register_30 (.D(WD), .en(and_30_out), .clk(clk), .Q(R30));  // open: clr
  Register #(.width(32)) register_31 (.D(WD), .en(and_31_out), .clk(clk), .Q(R31));  // open: clr
  Register #(.width(32)) register_32 (.D(WD), .en(and_32_out), .clk(clk), .Q(R32));  // open: clr
  Multiplexer #(.select(5), .width(32)) multiplexer_1 (
    .in0({32{1'b0}}), .in1(x1), .in2(x2), .in3(x3), .in4(x4), .in5(R6), .in6(R7), .in7(R8), .in8(R9),
    .in9(R10), .in10(R11), .in11(R12), .in12(R13), .in13(R14), .in14(R15), .in15(R16), .in16(R17),
    .in17(R18), .in18(R19), .in19(R20), .in20(R21), .in21(R22), .in22(R23), .in23(R24), .in24(R25),
    .in25(R26), .in26(R27), .in27(R28), .in28(R29), .in29(R30), .in30(R31), .in31(R32), .out(RD1), .sel(RR1));
  Multiplexer #(.select(5), .width(32)) multiplexer_2 (
    .in0({32{1'b0}}), .in1(x1), .in2(x2), .in3(x3), .in4(x4), .in5(R6), .in6(R7), .in7(R8), .in8(R9),
    .in9(R10), .in10(R11), .in11(R12), .in12(R13), .in13(R14), .in14(R15), .in15(R16), .in16(R17),
    .in17(R18), .in18(R19), .in19(R20), .in20(R21), .in21(R22), .in22(R23), .in23(R24), .in24(R25),
    .in25(R26), .in26(R27), .in27(R28), .in28(R29), .in29(R30), .in30(R31), .in31(R32), .out(RD2), .sel(RR2));

  // Other names for the same wires on the sheet: R2[31:0] = x1; R3[31:0] = x2; R4[31:0] = x3; R5[31:0] = x4
endmodule

module ALUcontrol (
  input  [6:0] op,
  input  [2:0] func3,
  input  [6:0] func7,
  output [2:0] S
);

  wire and_1_out, and_2_out, not_1_out, not_2_out;
  wire [2:0] bitstocontrol_1_s, multiplexer_1_out;

  not not_1 (not_1_out, op[6]);
  and and_1 (and_1_out, op[4], op[5], not_1_out);
  and and_2 (and_2_out, func7[5], and_1_out);
  bitsTocontrol bitstocontrol_1 (.func3(func3), .func7(and_2_out), .S(bitstocontrol_1_s));
  Multiplexer #(.width(3)) multiplexer_1 (.in0(3'b100), .in1(3'b101), .out(multiplexer_1_out), .sel(op[6]));
  Multiplexer #(.width(3)) multiplexer_2 (.in0(bitstocontrol_1_s), .in1(multiplexer_1_out), .out(S), .sel(not_2_out));
  not not_2 (not_2_out, op[4]);
endmodule

module bitsTocontrol (
  input  [2:0] func3,
  input  func7,
  output [2:0] S
);

  wire and_1_out, and_2_out, and_3_out, and_4_out, and_5_out, not_2_out, not_3_out;

  not not_1 (S[2], func3[2]);
  not not_2 (not_2_out, func3[1]);
  not not_3 (not_3_out, func3[0]);
  and and_1 (and_1_out, S[2], func3[1]);
  and and_2 (and_2_out, func3[2], not_2_out);
  and and_3 (and_3_out, S[2], not_2_out, func7);
  and and_4 (and_4_out, S[2], func3[0]);
  and and_5 (and_5_out, func3[2], func3[1], not_3_out);
  or or_1 (S[1], and_1_out, and_2_out);
  or or_2 (S[0], and_3_out, and_4_out, and_5_out);
endmodule

module Fowarding (
  input  [4:0] rs_ID_Ex,
  input  [4:0] rd_Ex_Mem,
  input  RegWr_Ex_Mem,
  input  [4:0] Mem_WB_rd,
  input  Mem_WB_RegWr,
  output [1:0] S2
);

  wire and_2_out, not_1_out, not_2_out, not_3_out, or_1_out, or_2_out, or_3_out, or_4_out;
  wire [4:0] xor_1_out, xor_2_out;

  or or_1 (or_1_out, rd_Ex_Mem[0], rd_Ex_Mem[1], rd_Ex_Mem[2], rd_Ex_Mem[3], rd_Ex_Mem[4]);
  assign xor_1_out = rd_Ex_Mem ^ rs_ID_Ex;  // XOR_Gate xor_1, 5 bits wide
  or or_2 (or_2_out, Mem_WB_rd[0], Mem_WB_rd[1], Mem_WB_rd[2], Mem_WB_rd[3], Mem_WB_rd[4]);
  assign xor_2_out = Mem_WB_rd ^ rs_ID_Ex;  // XOR_Gate xor_2, 5 bits wide
  not not_1 (not_1_out, or_3_out);
  or or_3 (or_3_out, xor_1_out[0], xor_1_out[1], xor_1_out[2], xor_1_out[3], xor_1_out[4]);
  not not_2 (not_2_out, or_4_out);
  or or_4 (or_4_out, xor_2_out[0], xor_2_out[1], xor_2_out[2], xor_2_out[3], xor_2_out[4]);
  and and_1 (S2[0], RegWr_Ex_Mem, or_1_out, not_1_out);
  and and_2 (and_2_out, Mem_WB_RegWr, or_2_out, not_2_out);
  not not_3 (not_3_out, S2[0]);
  and and_3 (S2[1], and_2_out, not_3_out);
endmodule

module FowardAB (
  input  [4:0] rs1_ID_Ex,
  input  [4:0] rs2_ID_Ex,
  input  [4:0] rd_Ex_Mem,
  input  [4:0] Mem_WB_rd,
  input  RegWr_Ex_Mem,
  input  Mem_WB_RegWr,
  output [1:0] Fa,
  output [1:0] Fb
);

  Fowarding fowarding_1 (
    .rs_ID_Ex(rs1_ID_Ex), .rd_Ex_Mem(rd_Ex_Mem), .RegWr_Ex_Mem(RegWr_Ex_Mem), .Mem_WB_rd(Mem_WB_rd),
    .Mem_WB_RegWr(Mem_WB_RegWr), .S2(Fa));
  Fowarding fowarding_2 (
    .rs_ID_Ex(rs2_ID_Ex), .rd_Ex_Mem(rd_Ex_Mem), .RegWr_Ex_Mem(RegWr_Ex_Mem), .Mem_WB_rd(Mem_WB_rd),
    .Mem_WB_RegWr(Mem_WB_RegWr), .S2(Fb));
endmodule

module HDU (
  input  [4:0] rs1_IF_ID,
  input  [4:0] rs2_IF_ID,
  input  [4:0] rd_ID_Ex,
  input  MemR_ID_EX,
  output Stall
);

  wire not_1_out, not_2_out, or_1_out, or_2_out, or_3_out, or_4_out;
  wire [4:0] xor_1_out, xor_2_out;

  assign xor_1_out = rs1_IF_ID ^ rd_ID_Ex;  // XOR_Gate xor_1, 5 bits wide
  assign xor_2_out = rd_ID_Ex ^ rs2_IF_ID;  // XOR_Gate xor_2, 5 bits wide
  or or_1 (or_1_out, rd_ID_Ex[0], rd_ID_Ex[1], rd_ID_Ex[2], rd_ID_Ex[3], rd_ID_Ex[4]);
  or or_2 (or_2_out, xor_1_out[0], xor_1_out[1], xor_1_out[2], xor_1_out[3], xor_1_out[4]);
  or or_3 (or_3_out, xor_2_out[0], xor_2_out[1], xor_2_out[2], xor_2_out[3], xor_2_out[4]);
  not not_1 (not_1_out, or_2_out);
  not not_2 (not_2_out, or_3_out);
  or or_4 (or_4_out, not_1_out, not_2_out);
  and and_1 (Stall, or_4_out, or_1_out, MemR_ID_EX);

  // Other names for the same wires on the sheet: rd_Ex_Mem[4:0] = rd_ID_Ex; rs1_ID_Ex[4:0] = rs1_IF_ID;
  //   rs2_ID_Ex[4:0] = rs2_IF_ID
endmodule

module ControlUnit (
  input  [6:0] op,
  output [7:0] flags
);

  wire and_1_out;
  wire [1:0] controlunitmux_1_s;
  wire [7:0] multiplexer_1_out;

  and and_1 (and_1_out, op[4], op[5]);
  Multiplexer #(.width(8)) multiplexer_1 (.in0(8'h21), .in1(8'h1), .out(multiplexer_1_out), .sel(and_1_out));
  Multiplexer #(.select(2), .width(8)) multiplexer_2 (
    .in0(multiplexer_1_out), .in1(8'h33), .in2(8'h68), .in3(8'h84), .out(flags), .sel(controlunitmux_1_s));
  ControlUnitMux controlunitmux_1 (.op(op[6:4]), .S(controlunitmux_1_s));
endmodule

module ControlUnitMux (
  input  [2:0] op,
  output [1:0] S
);

  wire and_2_out, not_1_out, not_2_out;

  not not_1 (not_1_out, op[1]);
  not not_2 (not_2_out, op[0]);
  and and_1 (S[1], op[1], not_2_out);
  and and_2 (and_2_out, not_1_out, not_2_out);
  or or_1 (S[0], and_2_out, op[2]);
endmodule
